# Fritzing sketch sunctl (saved by Fritzing 0.9.3b)
perfboards: 1

parts:
  Gizwits_WiFi_Witty_ESP-12F1 = Gizwits WiFi Witty ESP-12F
  J1 = female pin header, 8 pins [form="♀ (female)"]
  J2 = female pin header, 8 pins [form="♀ (female)"]
  R1 = Resistor [tolerance=±5% resistance=10k package=THT]
  R3 = Resistor [tolerance=±5% resistance=3.3k package=THT]
  J5 = female pin header, 2 pins [form="♀ (female)"]
  R4 = Photocell (LDR) [package=THT]
  reg = female pin header, 3 pins [form="♀ (female)"]
  S1 = Pushbutton [package="[THT]"]
  D1 = Rectifier Diode [part_number=1N4001 package="300 mil [THT]"]
  R5 = Resistor [tolerance=±5% resistance=10k package=THT]
  mode = female pin header, 2 pins [form="♀ (female)"]
  R6 = Resistor [tolerance=±5% resistance=10k package=THT]
  R7 = Resistor [tolerance=±5% resistance=10k package=THT]
  C1 = Ceramic Capacitor [capacitance=100nF package="100 mil [THT, multilayer]"]
  relay1 = female pin header, 1 pin [form="♀ (female)"]
  relay = female pin header, 1 pin [form="♀ (female)"]
  relay2 = female pin header, 1 pin [form="♀ (female)"]
  R2 = Resistor [tolerance=±5% resistance=3.3k package=THT]
  prog = female pin header, 3 pins [form="♀ (female)"]

nets:
  N1: Gizwits_WiFi_Witty_ESP-12F1.REST, J2.pin1, S1.Pin_3, S1.Pin_4, D1.anode, R5.Pin_0
  N2: Gizwits_WiFi_Witty_ESP-12F1.ADC, J2.pin2, R4.pin_0, R7.Pin_1, C1.0
  N3: Gizwits_WiFi_Witty_ESP-12F1.CH_PD, J2.pin3
  N4: Gizwits_WiFi_Witty_ESP-12F1.GPIO16, J2.pin4, D1.cathode
  N5: Gizwits_WiFi_Witty_ESP-12F1.GPIO14, J2.pin5
  N6: Gizwits_WiFi_Witty_ESP-12F1.GPIO12, J2.pin6
  N7: Gizwits_WiFi_Witty_ESP-12F1.GPIO13, J2.pin7
  3.3V: Gizwits_WiFi_Witty_ESP-12F1.VCC, J2.pin8, R1.Pin_0, reg.pin2, R5.Pin_1, R6.Pin_0, R7.Pin_0
  GND: Gizwits_WiFi_Witty_ESP-12F1.GND, J1.pin8, J5.pin1, R4.pin_1, reg.pin3, S1.Pin_1, S1.Pin_2, mode.pin2, C1.1, relay2.pin1, R2.Pin_1
  N8: Gizwits_WiFi_Witty_ESP-12F1.GPIO15, J1.pin7
  N9: Gizwits_WiFi_Witty_ESP-12F1.GPIO2, J1.pin6, R1.Pin_1
  N10: Gizwits_WiFi_Witty_ESP-12F1.GPIO0, J1.pin5, mode.pin1, R6.Pin_1
  N11: Gizwits_WiFi_Witty_ESP-12F1.GPIO4, J1.pin4
  ctrl: Gizwits_WiFi_Witty_ESP-12F1.GPIO5, J1.pin3, relay1.pin1
  N12: Gizwits_WiFi_Witty_ESP-12F1.RXD, J1.pin2, R3.Pin_1, R2.Pin_0
  N13: Gizwits_WiFi_Witty_ESP-12F1.TXD, J1.pin1, prog.pin1
  N14: R3.Pin_0, prog.pin2
  5V: J5.pin2, reg.pin1, relay.pin1, prog.pin3
